# Fritzing sketch skema (saved by Fritzing 0.9.3b)

parts:
  WeMos_D1_Mini1 = WeMos D1 Mini
  hc-sr1 = hc-sr04

nets:
  5V: WeMos_D1_Mini1.5V, hc-sr1.VCC
  N1: WeMos_D1_Mini1.D1, hc-sr1.Trig
  N2: WeMos_D1_Mini1.D2, hc-sr1.Echo
  N3: WeMos_D1_Mini1.G, hc-sr1.GND

notes:
  HC-SR04 ESP8266
  Vcc ----> 5V
  Gnd ----> G
  Trig ----> D1
  Echo ----> D2
